# Fritzing sketch FanController.00 (saved by Fritzing 0.9.2b)
circuit board: 8.11473cm x 2.80495cm
breadboards: 1

parts:
  Part1 = Arduino Nano (Rev3.0)
  J1 = COMPUTER-PERIPHERAL-POWER [package=computer-peripheral-power-ra]
  JP1 = Header 3 [package=molex-1x3_lock]
  Q1 = Basic FET P-Channel [package="TO220 [THT]"]
  R1 = Resistor [tolerance=±5% resistance=1k package=THT]
  C1 = Electrolytic Capacitor [capacitance=100µF voltage=16V package="200 mil [THT, electrolytic]"]
  D1 = Rectifier Diode [part_number=1N4001 package="300 mil [THT]"]
  T1 = LM35 Temperature Sensor [package="TO92 [THT]"]

nets:
  GND: Part1.GND, J1.GND, J1.NC, Q1.source, T1.GND
  N1: Part1.D3, R1.Pin_0
  VIN: Part1.VIN, J1.12V, JP1.2, C1.+, D1.cathode
  N2: Part1.5V, T1.+Vs
  N3: Part1.A1, T1.Vout
  N4: JP1.1, Q1.drain, C1.-, D1.anode
  N5: Q1.gate, R1.Pin_1
